# Fritzing sketch perpendicular hall effect sensor pair x4 (saved by Fritzing 0.9.2b)
circuit board: 2.79999cm x 2.79999cm
breadboards: 1

parts:
  J5 = female pin header, 3 pins [form="♀ (female)"]
  J8 = female pin header, 3 pins [form="♀ (female)"]
  J9 = female pin header, 3 pins [form="♀ (female)"]
  J10 = female pin header, 3 pins [form="♀ (female)"]
  J11 = female pin header, 3 pins [form="♀ (female)"]
  J12 = female pin header, 3 pins [form="♀ (female)"]
  J13 = female pin header, 3 pins [form="♀ (female)"]
  J14 = female pin header, 3 pins [form="♀ (female)"]
  J15 = female pin header, 4 pins [form="♀ (female)"]
  J16 = female pin header, 4 pins [form="♀ (female)"]
  J17 = female pin header, 4 pins [form="♀ (female)"]
  J18 = female pin header, 4 pins [form="♀ (female)"]

nets:
  N1: J5.pin1, J9.pin3, J16.pin1
  N2: J5.pin2, J9.pin2, J16.pin2
  N3: J5.pin3, J16.pin4
  N4: J8.pin1, J15.pin1
  N5: J8.pin2, J13.pin2, J15.pin3
  N6: J8.pin3, J13.pin3, J15.pin4
  N7: J9.pin1, J16.pin3
  N8: J10.pin1, J12.pin1, J17.pin1
  N9: J10.pin2, J12.pin2, J17.pin2
  N10: J10.pin3, J17.pin4
  N11: J11.pin1, J14.pin3, J18.pin4
  N12: J11.pin2, J14.pin2, J18.pin3
  N13: J11.pin3, J18.pin2
  N14: J12.pin3, J17.pin3
  N15: J13.pin1, J15.pin2
  N16: J14.pin1, J18.pin1

notes:
  V G D
  1 G V
  V G 1
  2 G V
  V G 1 2
