# Fritzing sketch single hall effect sensor x10 (saved by Fritzing 0.9.2b)
circuit board: 8.52cm x 1cm
breadboards: 1

parts:
  J9 = female pin header, 3 pins [form="♀ (female)"]
  J10 = longpad pin header, 3 pins [form="long pad"]
  J11 = female pin header, 3 pins [form="♀ (female)"]
  J12 = longpad pin header, 3 pins [form="long pad"]
  J13 = female pin header, 3 pins [form="♀ (female)"]
  J14 = female pin header, 3 pins [form="♀ (female)"]
  J15 = longpad pin header, 3 pins [form="long pad"]
  J16 = longpad pin header, 3 pins [form="long pad"]
  J17 = female pin header, 3 pins [form="♀ (female)"]
  J18 = female pin header, 3 pins [form="♀ (female)"]
  J19 = female pin header, 3 pins [form="♀ (female)"]
  J20 = female pin header, 3 pins [form="♀ (female)"]
  J21 = longpad pin header, 3 pins [form="long pad"]
  J22 = longpad pin header, 3 pins [form="long pad"]
  J23 = longpad pin header, 3 pins [form="long pad"]
  J24 = longpad pin header, 3 pins [form="long pad"]
  J25 = female pin header, 3 pins [form="♀ (female)"]
  J26 = female pin header, 3 pins [form="♀ (female)"]
  J27 = longpad pin header, 3 pins [form="long pad"]
  J28 = longpad pin header, 3 pins [form="long pad"]

nets:
  N1: J9.pin1, J10.pin1
  N2: J9.pin2, J10.pin2
  N3: J9.pin3, J10.pin3
  N4: J11.pin1, J12.pin1
  N5: J11.pin2, J12.pin2
  N6: J11.pin3, J12.pin3
  N7: J13.pin1, J16.pin1
  N8: J13.pin2, J16.pin2
  N9: J13.pin3, J16.pin3
  N10: J14.pin1, J15.pin1
  N11: J14.pin2, J15.pin2
  N12: J14.pin3, J15.pin3
  N13: J17.pin1, J22.pin1
  N14: J17.pin2, J22.pin2
  N15: J17.pin3, J22.pin3
  N16: J18.pin1, J23.pin1
  N17: J18.pin2, J23.pin2
  N18: J18.pin3, J23.pin3
  N19: J19.pin1, J21.pin1
  N20: J19.pin2, J21.pin2
  N21: J19.pin3, J21.pin3
  N22: J20.pin1, J24.pin1
  N23: J20.pin2, J24.pin2
  N24: J20.pin3, J24.pin3
  N25: J25.pin1, J27.pin1
  N26: J25.pin2, J27.pin2
  N27: J25.pin3, J27.pin3
  N28: J26.pin1, J28.pin1
  N29: J26.pin2, J28.pin2
  N30: J26.pin3, J28.pin3
